// Logisim project B2_G1.circ as structural Verilog: 2 circuits, main circuit DataMemory
module main (
  input  [3:0] Opcode,
  output RegDst,
  output Jump,
  output Branch,
  output MemRead,
  output MemtoReg,
  output [3:0] ALUop,
  output MemWrite,
  output ALUSrc,
  output RegWrite,
  output Shift
);

  wire [15:13] rom_1_data;

  ROM #(.addrWidth(4), .dataWidth(16)) rom_1 (
    .addr(Opcode),
    .data({rom_1_data, Shift, RegWrite, ALUSrc, MemWrite, ALUop, MemtoReg, MemRead, Branch, Jump, RegDst}));  // open: sel

  // Notes on the sheet:
  //   contents of rom_1 (hex, n*v repeats v):
  //   881 801 d00 861 c00 8c1 1821 1921 600 4 cc0 4 2 c80 c18 901
endmodule

module DataMemory (
  input  [3:0] Address,
  input  [3:0] WriteData,
  input  CLK,
  input  MemWrite,
  input  MemRead,
  output [3:0] ReadData
);

  RAM #(.addrWidth(4), .dataWidth(4), .bus("separate")) ram_1 (
    .addr(Address), .din(WriteData), .data(ReadData), .str(MemWrite), .clk(CLK), .ld(MemRead), .clr(1'b0));  // open: sel
endmodule
